# Fritzing sketch usbasp_pro-mini (saved by Fritzing 0.9.3b)

parts:
  Bauteil1 = Arduino Pro Mini (3.3V)
  J2 = Generic shrouded header - 10 pins [form="♂ (shrouded male)" package=THT]

nets:
  N1: Bauteil1.VCC, J2.pin6
  N2: Bauteil1.SCK, J2.pin2
  N3: Bauteil1.MISO, J2.pin1
  N4: Bauteil1.MOSI, J2.pin5
  N5: Bauteil1.GND, J2.pin10
  N6: Bauteil1.RESET, J2.pin3

custom parts:
  Generic shrouded header - 10 pins: Generic shrouded header
