# Fritzing sketch varioino_circuit_uno (saved by Fritzing 0.9.3b)
breadboards: 1

parts:
  Bauteil1 = Arduino Uno (Rev3)
  S1 = Pushbutton [package="[THT]"]
  Bauteil2 = BME280 Breakout
  J1 = Piezo Speaker
  R1 = Resistor [tolerance=±1% resistance=220 package=THT]
  Grove1 = Grove Infrared Receiver
  Grove1_2 = Grove Temperature Sensor
  Grove1_3 = Grove Light Sensor
  Grove1_4 = Grove OLED 128x96

nets:
  N1: Bauteil1.A4/SDA, Bauteil2.SDI/SDA
  N2: Bauteil1.A5/SCL, Bauteil2.SCK/SCL
  N3: Bauteil1.D9_PWM, J1.pin2, R1.Pin_0, R1.Pin_1
  N4: Bauteil1.D10_PWM/SS, J1.pin1
  N5: Bauteil1.D13/SCK, S1.Pin_3, S1.Pin_4
  GND: Bauteil1.GND, S1.Pin_1, S1.Pin_2, Bauteil2.GND, Grove1.GND, Grove1_2.GND, Grove1_3.GND, Grove1_4.GND
  VCC: Bauteil1.3V3, Bauteil2.3.3V, Grove1.VCC, Grove1_2.VCC, Grove1_3.VCC, Grove1_4.VCC
